// Logisim project final.circ as structural Verilog
module fa (
  input  A,
  input  B,
  input  C,
  output Sum,
  output Cout
);

  wire and_1_out, and_2_out, xor_1_out;

  and and_1 (and_1_out, A, B);
  xor xor_1 (xor_1_out, A, B);
  xor xor_2 (Sum, xor_1_out, C);
  and and_2 (and_2_out, xor_1_out, C);
  or or_1 (Cout, and_2_out, and_1_out);
endmodule

module is_2 (
  input  TL,
  input  T,
  input  TR,
  input  L,
  input  R,
  input  B,
  input  BL,
  input  BR,
  output is_2
);

  wire and_1_out, and_2_out, and_3_out, and_4_out, and_5_out, and_6_out, and_7_out, and_8_out, and_9_out,
       and_10_out, and_11_out, and_12_out, and_13_out, and_14_out, and_15_out, and_16_out, and_17_out,
       and_18_out, and_19_out, and_20_out, and_21_out, and_22_out, and_23_out, and_24_out, and_25_out,
       and_26_out, and_27_out, and_28_out;

  and and_1 (and_1_out, TL, T);
  and and_2 (and_2_out, TL, TR);
  and and_3 (and_3_out, T, L);
  and and_4 (and_4_out, T, TR);
  and and_5 (and_5_out, TL, L);
  and and_6 (and_6_out, TL, R);
  and and_7 (and_7_out, T, R);
  and and_8 (and_8_out, TR, R);
  and and_9 (and_9_out, TR, L);
  and and_10 (and_10_out, L, R);
  and and_11 (and_11_out, TL, B);
  and and_12 (and_12_out, TL, BL);
  and and_13 (and_13_out, T, B);
  and and_14 (and_14_out, T, BL);
  and and_15 (and_15_out, TR, B);
  and and_16 (and_16_out, L, B);
  and and_17 (and_17_out, R, B);
  and and_18 (and_18_out, TL, BR);
  and and_19 (and_19_out, T, BR);
  and and_20 (and_20_out, TR, BL);
  and and_21 (and_21_out, TR, BR);
  and and_22 (and_22_out, L, BL);
  and and_23 (and_23_out, L, BR);
  and and_24 (and_24_out, R, BR);
  and and_25 (and_25_out, R, BL);
  and and_26 (and_26_out, B, BR);
  and and_27 (and_27_out, B, BL);
  and and_28 (and_28_out, BL, BR);
  ExactlyOne xor_1 (
    .out(is_2), .in0(and_5_out), .in1(and_27_out), .in2(and_26_out), .in3(and_17_out), .in4(and_25_out),
    .in5(and_24_out), .in6(and_10_out), .in7(and_16_out), .in8(and_22_out), .in9(and_23_out),
    .in10(and_9_out), .in11(and_8_out), .in12(and_15_out), .in13(and_20_out), .in14(and_4_out),
    .in15(and_3_out), .in16(and_7_out), .in17(and_13_out), .in18(and_14_out), .in19(and_19_out),
    .in20(and_1_out), .in21(and_2_out), .in22(and_6_out), .in23(and_11_out), .in24(and_12_out),
    .in25(and_18_out), .in26(and_21_out), .in27(and_28_out));
endmodule

module \cell  (
  input  T,
  input  TR,
  input  TL,
  input  L,
  input  R,
  input  on,
  input  BR,
  input  BL,
  input  B,
  output Alive
);

  wire cellstats_1_b, cellstats_1_bl_2, cellstats_1_br, cellstats_1_l, cellstats_1_r, cellstats_1_t,
       cellstats_1_tl, cellstats_1_tr, clock_1_out, is_2_1_is_2, is_3_1_is_3, is_3_2_is_3, multiplexer_1_out,
       multiplexer_2_out, or_1_out;

  is_3 is_3_1 (
    .TL(cellstats_1_tl), .T(cellstats_1_t), .TR(cellstats_1_tr), .L(cellstats_1_l), .R(cellstats_1_r),
    .BL(cellstats_1_bl_2), .B(cellstats_1_b), .BR(cellstats_1_br), .is_3(is_3_1_is_3));
  CellStats cellstats_1 (
    .B(cellstats_1_b), .BR(cellstats_1_br), .TL(cellstats_1_tl), .T(cellstats_1_t), .TR(cellstats_1_tr),
    .L(cellstats_1_l), .R(cellstats_1_r), .BL_2(cellstats_1_bl_2), .TLin(TL), .Tin(T), .TRin(TR), .Lin(L),
    .Rin(R), .BL(BL), .Bin(B), .BRin(BR));
  Multiplexer #(.enable("false")) multiplexer_1 (
    .in0(is_3_1_is_3), .in1(or_1_out), .out(multiplexer_1_out), .sel(Alive));
  Multiplexer #(.enable("false")) multiplexer_2 (
    .in0(multiplexer_1_out), .in1(1'b1), .out(multiplexer_2_out), .sel(on));
  D_Flip_Flop d_ff_1 (.clk(clock_1_out), .D(multiplexer_2_out), .Q(Alive));  // open: Qn, preset, en, reset
  Clock clock_1 (.out(clock_1_out));
  is_2 is_2_1 (
    .TL(cellstats_1_tl), .T(cellstats_1_t), .TR(cellstats_1_tr), .L(cellstats_1_l), .R(cellstats_1_r),
    .B(cellstats_1_b), .BL(cellstats_1_bl_2), .BR(cellstats_1_br), .is_2(is_2_1_is_2));
  is_3 is_3_2 (
    .TL(cellstats_1_tl), .T(cellstats_1_t), .TR(cellstats_1_tr), .L(cellstats_1_l), .R(cellstats_1_r),
    .BL(cellstats_1_bl_2), .B(cellstats_1_b), .BR(cellstats_1_br), .is_3(is_3_2_is_3));
  or or_1 (or_1_out, is_2_1_is_2, is_3_2_is_3);
endmodule

module CellStats (
  input  TLin,
  input  Tin,
  input  TRin,
  input  Lin,
  input  Rin,
  input  BL,
  input  Bin,
  input  BRin,
  output B,
  output BR,
  output TL,
  output T,
  output TR,
  output L,
  output R,
  output BL_2
);

  wire clock_1_out;

  Clock clock_1 (.out(clock_1_out));

  assign B = Bin;
  assign BL_2 = BL;
  assign BR = BRin;
  assign L = Lin;
  assign R = Rin;
  assign T = Tin;
  assign TL = TLin;
  assign TR = TRin;
endmodule

module is_3 (
  input  TL,
  input  T,
  input  TR,
  input  L,
  input  R,
  input  BL,
  input  B,
  input  BR,
  output is_3
);

  wire and_1_out, and_2_out, and_3_out, and_4_out, and_5_out, and_6_out, and_7_out, and_8_out, and_9_out,
       and_10_out, and_11_out, and_12_out, and_13_out, and_14_out, and_15_out, and_16_out, and_17_out,
       and_18_out, and_19_out, and_20_out, and_21_out, and_22_out, and_23_out, and_24_out, and_25_out,
       and_26_out, and_27_out, and_28_out, and_29_out, and_30_out, and_31_out, and_32_out, and_33_out,
       and_34_out, and_35_out, and_36_out, and_37_out, and_38_out, and_39_out, and_40_out, and_41_out,
       and_42_out, and_43_out, and_44_out, and_45_out, and_46_out, and_47_out, and_48_out, and_49_out,
       and_50_out, and_51_out, and_52_out, and_53_out, and_54_out, and_55_out, and_56_out, xor_1_out,
       xor_2_out, xor_3_out, xor_4_out, xor_5_out, xor_6_out, xor_7_out, xor_8_out, xor_9_out, xor_10_out,
       xor_11_out, xor_12_out, xor_13_out, xor_14_out, xor_15_out, xor_16_out, xor_17_out, xor_18_out,
       xor_19_out, xor_20_out, xor_21_out, xor_22_out, xor_23_out, xor_24_out, xor_25_out, xor_26_out,
       xor_27_out, xor_28_out, xor_29_out, xor_30_out, xor_31_out, xor_32_out, xor_33_out, xor_34_out,
       xor_35_out, xor_36_out, xor_37_out, xor_38_out, xor_39_out, xor_40_out, xor_41_out, xor_42_out,
       xor_43_out, xor_44_out, xor_45_out, xor_46_out, xor_47_out, xor_48_out, xor_49_out, xor_50_out,
       xor_51_out, xor_52_out, xor_53_out, xor_54_out;

  and and_1 (and_1_out, TL, T, TR);
  and and_2 (and_2_out, TL, T, L);
  and and_3 (and_3_out, TL, T, R);
  and and_4 (and_4_out, TL, T, BL);
  and and_5 (and_5_out, TL, T, B);
  and and_6 (and_6_out, TL, T, BR);
  and and_7 (and_7_out, TL, TR, L);
  and and_8 (and_8_out, TL, TR, R);
  and and_9 (and_9_out, TL, TR, BL);
  and and_10 (and_10_out, TL, TR, B);
  and and_11 (and_11_out, TL, TR, BR);
  and and_12 (and_12_out, TL, L, R);
  and and_13 (and_13_out, TL, L, BL);
  and and_14 (and_14_out, TL, L, B);
  and and_15 (and_15_out, TL, L, BR);
  and and_16 (and_16_out, TL, R, BL);
  and and_17 (and_17_out, TL, R, B);
  and and_18 (and_18_out, TL, R, BR);
  and and_19 (and_19_out, TL, BL, B);
  and and_20 (and_20_out, TL, BL, BR);
  and and_21 (and_21_out, TL, B, BR);
  and and_22 (and_22_out, T, TR, L);
  and and_23 (and_23_out, T, TR, R);
  and and_24 (and_24_out, T, TR, BL);
  and and_25 (and_25_out, T, TR, B);
  and and_26 (and_26_out, T, TR, BR);
  and and_27 (and_27_out, T, L, R);
  and and_28 (and_28_out, T, L, BL);
  and and_29 (and_29_out, T, L, B);
  and and_30 (and_30_out, T, L, BR);
  and and_31 (and_31_out, T, R, BL);
  and and_32 (and_32_out, T, R, B);
  and and_33 (and_33_out, T, R, BR);
  and and_34 (and_34_out, T, BL, B);
  and and_35 (and_35_out, T, BL, BR);
  and and_36 (and_36_out, T, B, BR);
  and and_37 (and_37_out, TR, L, R);
  and and_38 (and_38_out, TR, L, BL);
  and and_39 (and_39_out, TR, L, B);
  and and_40 (and_40_out, TR, L, BR);
  and and_41 (and_41_out, TR, R, BL);
  and and_42 (and_42_out, TR, R, B);
  and and_43 (and_43_out, TR, R, BR);
  and and_44 (and_44_out, TR, BL, B);
  and and_45 (and_45_out, TR, BL, BR);
  and and_46 (and_46_out, TR, B, BR);
  and and_47 (and_47_out, L, R, BL);
  and and_48 (and_48_out, L, R, B);
  and and_49 (and_49_out, L, R, BR);
  and and_50 (and_50_out, L, BL, B);
  and and_51 (and_51_out, L, BL, BR);
  and and_52 (and_52_out, L, B, BR);
  and and_53 (and_53_out, R, BL, B);
  and and_54 (and_54_out, R, BL, BR);
  and and_55 (and_55_out, R, B, BR);
  and and_56 (and_56_out, BL, B, BR);
  xor xor_1 (xor_1_out, and_53_out, and_37_out);
  xor xor_2 (xor_2_out, xor_1_out, and_38_out);
  xor xor_3 (xor_3_out, xor_2_out, and_1_out);
  xor xor_4 (xor_4_out, xor_3_out, and_2_out);
  xor xor_5 (xor_5_out, xor_4_out, and_3_out);
  xor xor_6 (xor_6_out, xor_5_out, and_4_out);
  xor xor_7 (xor_7_out, xor_6_out, and_5_out);
  xor xor_8 (xor_8_out, xor_7_out, and_6_out);
  xor xor_9 (xor_9_out, xor_8_out, and_7_out);
  xor xor_10 (xor_10_out, xor_9_out, and_8_out);
  xor xor_11 (xor_11_out, xor_10_out, and_9_out);
  xor xor_12 (xor_12_out, xor_11_out, and_10_out);
  xor xor_13 (xor_13_out, xor_12_out, and_11_out);
  xor xor_14 (xor_14_out, xor_13_out, and_12_out);
  xor xor_15 (xor_15_out, xor_14_out, and_13_out);
  xor xor_16 (xor_16_out, xor_15_out, and_14_out);
  xor xor_17 (xor_17_out, xor_16_out, and_15_out);
  xor xor_18 (xor_18_out, xor_17_out, and_16_out);
  xor xor_19 (xor_19_out, xor_18_out, and_54_out);
  xor xor_20 (xor_20_out, xor_19_out, and_17_out);
  xor xor_21 (xor_21_out, xor_20_out, and_18_out);
  xor xor_22 (xor_22_out, xor_21_out, and_19_out);
  xor xor_23 (xor_23_out, xor_22_out, and_20_out);
  xor xor_24 (xor_24_out, xor_23_out, and_21_out);
  xor xor_25 (xor_25_out, xor_24_out, and_22_out);
  xor xor_26 (xor_26_out, xor_25_out, and_23_out);
  xor xor_27 (xor_27_out, xor_26_out, and_24_out);
  xor xor_28 (xor_28_out, xor_27_out, and_25_out);
  xor xor_29 (xor_29_out, xor_28_out, and_26_out);
  xor xor_30 (xor_30_out, xor_29_out, and_27_out);
  xor xor_31 (xor_31_out, xor_30_out, and_28_out);
  xor xor_32 (xor_32_out, xor_31_out, and_29_out);
  xor xor_33 (xor_33_out, xor_32_out, and_30_out);
  xor xor_34 (xor_34_out, xor_33_out, and_31_out);
  xor xor_35 (xor_35_out, xor_34_out, and_32_out);
  xor xor_36 (xor_36_out, xor_35_out, and_33_out);
  xor xor_37 (xor_37_out, xor_36_out, and_34_out);
  xor xor_38 (xor_38_out, xor_37_out, and_35_out);
  xor xor_39 (xor_39_out, xor_38_out, and_36_out);
  xor xor_40 (xor_40_out, xor_39_out, and_39_out);
  xor xor_41 (xor_41_out, xor_40_out, and_40_out);
  xor xor_42 (xor_42_out, xor_41_out, and_55_out);
  xor xor_43 (xor_43_out, xor_42_out, and_42_out);
  xor xor_44 (xor_44_out, xor_43_out, and_43_out);
  xor xor_45 (xor_45_out, xor_44_out, and_44_out);
  xor xor_46 (xor_46_out, xor_45_out, and_45_out);
  xor xor_47 (xor_47_out, xor_46_out, and_46_out);
  xor xor_48 (xor_48_out, xor_47_out, and_47_out);
  xor xor_49 (xor_49_out, xor_48_out, and_48_out);
  xor xor_50 (xor_50_out, xor_49_out, and_49_out);
  xor xor_51 (xor_51_out, xor_50_out, and_50_out);
  xor xor_52 (xor_52_out, xor_51_out, and_51_out);
  xor xor_53 (xor_53_out, xor_52_out, and_52_out);
  xor xor_54 (xor_54_out, xor_53_out, and_41_out);
  xor xor_55 (is_3, xor_54_out, and_56_out);
endmodule

module cellmatrix (
  input  in_1,
  input  in_2
);

  wire _1_1, _1_2, _1_3, _1_4, _1_5, _1_6, _1_7, _1_8, _2_1, _2_2, _2_3, _2_4, _2_5, _2_6, _2_7, _2_8, _3_1,
       _3_2, _3_3, _3_4, _3_5, _3_6, _3_7, _3_8, _4_1, _4_2, _4_3, _4_4, _4_5, _4_6, _4_7, _4_8, _5_1, _5_2,
       _5_3, _5_4, _5_5, _5_6, _5_7, _5_8, _6_1, _6_2, _6_3, _6_4, _6_5, _6_6, _6_7, _6_8, _7_1, _7_2, _7_3,
       _7_4, _7_5, _7_6, _7_7, _7_8, _8_1, _8_2, _8_3, _8_4, _8_5, _8_6, _8_7, _8_8, clock_1_out, on1;

  \cell  cell_1 (
    .L(_1_8), .TL(_8_8), .T(_8_1), .TR(_8_2), .BL(_2_8), .B(_2_1), .Alive(_1_1), .BR(_2_2), .R(_1_2),
    .on(in_2));
  \cell  cell_2 (
    .L(_2_8), .TL(_1_8), .T(_1_1), .TR(_1_2), .BL(_3_8), .B(_3_2), .Alive(_2_1), .BR(_3_2), .R(_2_2),
    .on(in_2));
  \cell  cell_3 (
    .L(_3_8), .TL(_2_8), .T(_2_1), .TR(_2_2), .BL(_4_8), .B(_4_1), .Alive(_3_1), .BR(_4_2), .R(_3_2),
    .on(in_2));
  \cell  cell_4 (
    .L(_4_8), .TL(_3_8), .T(_3_1), .TR(_3_2), .BL(_5_8), .B(_5_1), .Alive(_4_1), .BR(_5_2), .R(_4_2),
    .on(in_2));
  \cell  cell_5 (
    .L(_5_8), .TL(_4_8), .T(_4_1), .TR(_4_2), .BL(_6_8), .B(_6_1), .Alive(_5_1), .BR(_6_2), .R(_5_2),
    .on(in_2));
  \cell  cell_6 (
    .L(_6_8), .TL(_5_8), .T(_5_1), .TR(_5_2), .BL(_7_8), .B(_7_1), .Alive(_6_1), .BR(_7_2), .R(_6_2),
    .on(in_2));
  \cell  cell_7 (
    .L(_7_8), .TL(_6_8), .T(_6_1), .TR(_6_2), .BL(_8_8), .B(_8_1), .Alive(_7_1), .BR(_8_2), .R(_7_2), .on(on1));
  \cell  cell_8 (
    .L(_8_8), .TL(_7_8), .T(_7_1), .TR(_7_2), .BL(_1_8), .B(_1_1), .Alive(_8_1), .BR(_1_2), .R(_8_2), .on(on1));
  \cell  cell_9 (
    .L(_1_1), .TL(_8_1), .T(_8_2), .TR(_8_3), .BL(_2_1), .B(_2_2), .Alive(_1_2), .BR(_2_3), .R(_1_3),
    .on(in_2));
  \cell  cell_10 (
    .L(_2_1), .TL(_1_1), .T(_1_2), .TR(_1_3), .BL(_3_1), .B(_3_2), .Alive(_2_2), .BR(_3_3), .R(_2_3),
    .on(in_2));
  \cell  cell_11 (
    .L(_3_1), .TL(_2_1), .T(_2_2), .TR(_2_3), .BL(_4_1), .B(_4_2), .Alive(_3_2), .BR(_4_3), .R(_3_3), .on(on1));
  \cell  cell_12 (
    .L(_4_1), .TL(_3_1), .T(_3_2), .TR(_3_3), .BL(_5_1), .B(_5_2), .Alive(_4_2), .BR(_5_3), .R(_4_3), .on(on1));
  \cell  cell_13 (
    .L(_5_1), .TL(_4_1), .T(_4_2), .TR(_4_3), .BL(_6_1), .B(_6_2), .Alive(_5_2), .BR(_6_3), .R(_5_3), .on(on1));
  \cell  cell_14 (
    .L(_6_1), .TL(_5_1), .T(_5_2), .TR(_5_3), .BL(_7_1), .B(_7_2), .Alive(_6_2), .BR(_7_3), .R(_6_3),
    .on(in_2));
  \cell  cell_15 (
    .L(_7_1), .TL(_6_1), .T(_6_2), .TR(_6_3), .BL(_8_1), .B(_8_2), .Alive(_7_2), .BR(_8_3), .R(_7_3),
    .on(in_2));
  \cell  cell_16 (
    .L(_8_1), .TL(_7_1), .T(_7_2), .TR(_7_3), .BL(_1_1), .B(_1_2), .Alive(_8_2), .BR(_1_3), .R(_8_3), .on(on1));
  \cell  cell_17 (
    .L(_2_2), .TL(_1_2), .T(_1_3), .TR(_1_4), .BL(_3_2), .B(_3_3), .Alive(_2_3), .BR(_3_4), .R(_2_4),
    .on(in_2));
  \cell  cell_18 (
    .L(_3_2), .TL(_2_2), .T(_2_3), .TR(_2_4), .BL(_4_2), .B(_4_3), .Alive(_3_3), .BR(_4_4), .R(_3_4),
    .on(in_2));
  \cell  cell_19 (
    .L(_4_2), .TL(_3_2), .T(_3_3), .TR(_3_4), .BL(_5_2), .B(_5_3), .Alive(_4_3), .BR(_5_4), .R(_4_4),
    .on(in_2));
  \cell  cell_20 (
    .L(_5_2), .TL(_4_2), .T(_4_3), .TR(_4_4), .BL(_6_2), .B(_6_3), .Alive(_5_3), .BR(_6_4), .R(_5_4),
    .on(in_2));
  \cell  cell_21 (
    .L(_6_2), .TL(_5_2), .T(_5_3), .TR(_5_4), .BL(_7_2), .B(_7_3), .Alive(_6_3), .BR(_7_4), .R(_6_4), .on(on1));
  \cell  cell_22 (
    .L(_7_2), .TL(_6_2), .T(_6_3), .TR(_6_4), .BL(_8_2), .B(_8_3), .Alive(_7_3), .BR(_8_4), .R(_7_4), .on(on1));
  \cell  cell_23 (
    .L(_1_2), .TL(_8_2), .T(_8_3), .TR(_8_4), .BL(_2_2), .B(_2_3), .Alive(_1_3), .BR(_2_4), .R(_1_4),
    .on(in_2));
  \cell  cell_24 (
    .L(_8_2), .TL(_7_2), .T(_7_3), .TR(_7_4), .BL(_1_2), .B(_1_3), .Alive(_8_3), .BR(_1_4), .R(_8_4),
    .on(in_2));
  \cell  cell_25 (
    .L(_1_3), .TL(_8_3), .T(_8_4), .TR(_8_5), .BL(_2_3), .B(_2_4), .Alive(_1_4), .BR(_2_5), .R(_1_5),
    .on(in_2));
  \cell  cell_26 (
    .L(_2_3), .TL(_1_3), .T(_1_4), .TR(_1_5), .BL(_3_3), .B(_3_4), .Alive(_2_4), .BR(_3_5), .R(_2_5), .on(on1));
  \cell  cell_27 (
    .L(_3_3), .TL(_2_3), .T(_2_4), .TR(_2_5), .BL(_4_3), .B(_4_4), .Alive(_3_4), .BR(_4_5), .R(_3_5),
    .on(in_2));
  \cell  cell_28 (
    .L(_4_3), .TL(_3_3), .T(_3_4), .TR(_3_5), .BL(_5_3), .B(_5_4), .Alive(_4_4), .BR(_5_5), .R(_4_5),
    .on(in_2));
  \cell  cell_29 (
    .L(_5_3), .TL(_4_3), .T(_4_4), .TR(_4_5), .BL(_6_3), .B(_6_4), .Alive(_5_4), .BR(_6_5), .R(_5_5),
    .on(in_2));
  \cell  cell_30 (
    .L(_6_3), .TL(_5_3), .T(_5_4), .TR(_5_5), .BL(_7_3), .B(_7_4), .Alive(_6_4), .BR(_7_5), .R(_6_5),
    .on(in_2));
  \cell  cell_31 (
    .L(_7_3), .TL(_6_3), .T(_6_4), .TR(_6_5), .BL(_8_3), .B(_8_4), .Alive(_7_4), .BR(_8_5), .R(_7_5),
    .on(in_2));
  \cell  cell_32 (
    .L(_8_3), .TL(_7_3), .T(_7_4), .TR(_7_5), .BL(_1_3), .B(_1_4), .Alive(_8_4), .BR(_1_5), .R(_8_5),
    .on(in_2));
  \cell  cell_33 (
    .L(_1_4), .TL(_8_4), .T(_8_5), .TR(_8_6), .BL(_2_4), .B(_2_5), .Alive(_1_5), .BR(_2_6), .R(_1_6),
    .on(in_2));
  \cell  cell_34 (
    .L(_2_4), .TL(_1_4), .T(_1_5), .TR(_1_6), .BL(_3_4), .B(_3_5), .Alive(_2_5), .BR(_3_6), .R(_2_6), .on(on1));
  \cell  cell_35 (
    .L(_3_4), .TL(_2_4), .T(_2_5), .TR(_2_6), .BL(_4_4), .B(_4_5), .Alive(_3_5), .BR(_4_6), .R(_3_6),
    .on(in_2));
  \cell  cell_36 (
    .L(_4_4), .TL(_3_4), .T(_3_5), .TR(_3_6), .BL(_5_4), .B(_5_5), .Alive(_4_5), .BR(_5_6), .R(_4_6),
    .on(in_2));
  \cell  cell_37 (
    .L(_5_4), .TL(_4_4), .T(_4_5), .TR(_4_6), .BL(_6_4), .B(_6_5), .Alive(_5_5), .BR(_6_6), .R(_5_6),
    .on(in_2));
  \cell  cell_38 (
    .L(_6_4), .TL(_5_4), .T(_5_5), .TR(_5_6), .BL(_7_4), .B(_7_5), .Alive(_6_5), .BR(_7_6), .R(_6_6),
    .on(in_2));
  \cell  cell_39 (
    .L(_7_4), .TL(_6_4), .T(_6_5), .TR(_6_6), .BL(_8_4), .B(_8_5), .Alive(_7_5), .BR(_8_6), .R(_7_6),
    .on(in_2));
  \cell  cell_40 (
    .L(_8_4), .TL(_7_4), .T(_7_5), .TR(_7_6), .BL(_1_4), .B(_1_5), .Alive(_8_5), .BR(_1_6), .R(_8_6),
    .on(in_2));
  \cell  cell_41 (
    .L(_2_5), .TL(_1_5), .T(_1_6), .TR(_1_7), .BL(_3_5), .B(_3_6), .Alive(_2_6), .BR(_3_7), .R(_2_7),
    .on(in_2));
  \cell  cell_42 (
    .L(_3_5), .TL(_2_5), .T(_2_6), .TR(_2_7), .BL(_4_5), .B(_4_6), .Alive(_3_6), .BR(_4_7), .R(_3_7),
    .on(in_2));
  \cell  cell_43 (
    .L(_4_5), .TL(_3_5), .T(_3_6), .TR(_3_7), .BL(_5_5), .B(_5_6), .Alive(_4_6), .BR(_5_7), .R(_4_7),
    .on(in_2));
  \cell  cell_44 (
    .L(_5_5), .TL(_4_5), .T(_4_6), .TR(_4_7), .BL(_6_5), .B(_6_6), .Alive(_5_6), .BR(_6_7), .R(_5_7),
    .on(in_2));
  \cell  cell_45 (
    .L(_6_5), .TL(_5_5), .T(_5_6), .TR(_5_7), .BL(_7_5), .B(_7_6), .Alive(_6_6), .BR(_7_7), .R(_6_7), .on(on1));
  \cell  cell_46 (
    .L(_7_5), .TL(_6_5), .T(_6_6), .TR(_6_7), .BL(_8_5), .B(_8_6), .Alive(_7_6), .BR(_8_7), .R(_7_7), .on(on1));
  \cell  cell_47 (
    .L(_1_5), .TL(_8_5), .T(_8_6), .TR(_8_7), .BL(_2_5), .B(_2_6), .Alive(_1_6), .BR(_2_7), .R(_1_7),
    .on(in_2));
  \cell  cell_48 (
    .L(_8_5), .TL(_7_5), .T(_7_6), .TR(_7_7), .BL(_1_5), .B(_1_6), .Alive(_8_6), .BR(_1_7), .R(_8_7),
    .on(in_2));
  \cell  cell_49 (
    .L(_1_6), .TL(_8_6), .T(_8_7), .TR(_8_8), .BL(_2_6), .B(_2_7), .Alive(_1_7), .BR(_2_8), .R(_1_8),
    .on(in_2));
  \cell  cell_50 (
    .L(_2_6), .TL(_1_6), .T(_1_7), .TR(_1_8), .BL(_3_6), .B(_3_7), .Alive(_2_7), .BR(_3_8), .R(_2_8),
    .on(in_2));
  \cell  cell_51 (
    .L(_3_6), .TL(_2_6), .T(_2_7), .TR(_2_8), .BL(_4_6), .B(_4_7), .Alive(_3_7), .BR(_4_8), .R(_3_8), .on(on1));
  \cell  cell_52 (
    .L(_4_6), .TL(_3_6), .T(_3_7), .TR(_3_8), .BL(_5_6), .B(_5_7), .Alive(_4_7), .BR(_5_8), .R(_4_8), .on(on1));
  \cell  cell_53 (
    .L(_5_6), .TL(_4_6), .T(_4_7), .TR(_4_8), .BL(_6_6), .B(_6_7), .Alive(_5_7), .BR(_6_8), .R(_5_8), .on(on1));
  \cell  cell_54 (
    .L(_6_6), .TL(_5_6), .T(_5_7), .TR(_5_8), .BL(_7_6), .B(_7_7), .Alive(_6_7), .BR(_7_8), .R(_6_8),
    .on(in_2));
  \cell  cell_55 (
    .L(_7_6), .TL(_6_6), .T(_6_7), .TR(_6_8), .BL(_8_6), .B(_8_7), .Alive(_7_7), .BR(_8_8), .R(_7_8),
    .on(in_2));
  \cell  cell_56 (
    .L(_8_6), .TL(_7_6), .T(_7_7), .TR(_7_8), .BL(_1_6), .B(_1_7), .Alive(_8_7), .BR(_1_8), .R(_8_8), .on(on1));
  \cell  cell_57 (
    .L(_1_7), .TL(_8_7), .T(_8_8), .TR(_8_1), .BL(_2_7), .B(_2_8), .Alive(_1_8), .BR(_2_1), .R(_1_1),
    .on(in_2));
  \cell  cell_58 (
    .L(_2_7), .TL(_1_7), .T(_1_8), .TR(_1_1), .BL(_3_7), .B(_3_8), .Alive(_2_8), .BR(_3_1), .R(_2_1),
    .on(in_2));
  \cell  cell_59 (
    .L(_3_7), .TL(_2_7), .T(_2_8), .TR(_2_1), .BL(_4_7), .B(_4_8), .Alive(_3_8), .BR(_4_1), .R(_3_1),
    .on(in_2));
  \cell  cell_60 (
    .L(_4_7), .TL(_3_7), .T(_3_8), .TR(_3_1), .BL(_5_7), .B(_5_8), .Alive(_4_8), .BR(_5_1), .R(_4_1),
    .on(in_2));
  \cell  cell_61 (
    .L(_5_7), .TL(_4_7), .T(_4_8), .TR(_4_1), .BL(_6_7), .B(_6_8), .Alive(_5_8), .BR(_6_1), .R(_5_1),
    .on(in_2));
  \cell  cell_62 (
    .L(_6_7), .TL(_5_7), .T(_5_8), .TR(_5_1), .BL(_7_7), .B(_7_8), .Alive(_6_8), .BR(_7_1), .R(_6_1),
    .on(in_2));
  \cell  cell_63 (
    .L(_7_7), .TL(_6_7), .T(_6_8), .TR(_6_1), .BL(_8_7), .B(_8_8), .Alive(_7_8), .BR(_8_1), .R(_7_1), .on(on1));
  \cell  cell_64 (
    .L(_8_7), .TL(_7_7), .T(_7_8), .TR(_7_1), .BL(_1_7), .B(_1_8), .Alive(_8_8), .BR(_1_1), .R(_8_1), .on(on1));
  Clock clock_1 (.out(clock_1_out));
  LED led_1 (.in(_1_1));
  LED led_2 (.in(_2_1));
  LED led_3 (.in(_3_1));
  LED led_4 (.in(_4_1));
  LED led_5 (.in(_5_1));
  LED led_6 (.in(_6_1));
  LED led_7 (.in(_7_1));
  LED led_8 (.in(_8_1));
  D_Flip_Flop d_ff_1 (.clk(clock_1_out), .D(in_1), .Q(on1), .en(clock_1_out));  // open: Qn, preset, reset
  LED led_9 (.in(_1_2));
  LED led_10 (.in(_2_2));
  LED led_11 (.in(_3_2));
  LED led_12 (.in(_4_2));
  LED led_13 (.in(_5_2));
  LED led_14 (.in(_6_2));
  LED led_15 (.in(_7_2));
  LED led_16 (.in(_8_2));
  LED led_17 (.in(_1_4));
  LED led_18 (.in(_1_3));
  LED led_19 (.in(_2_3));
  LED led_20 (.in(_2_4));
  LED led_21 (.in(_3_3));
  LED led_22 (.in(_3_4));
  LED led_23 (.in(_4_3));
  LED led_24 (.in(_4_4));
  LED led_25 (.in(_5_4));
  LED led_26 (.in(_5_3));
  LED led_27 (.in(_6_4));
  LED led_28 (.in(_6_3));
  LED led_29 (.in(_7_4));
  LED led_30 (.in(_7_3));
  LED led_31 (.in(_8_3));
  LED led_32 (.in(_8_4));
  LED led_33 (.in(_1_5));
  LED led_34 (.in(_2_5));
  LED led_35 (.in(_3_5));
  LED led_36 (.in(_4_5));
  LED led_37 (.in(_5_5));
  LED led_38 (.in(_6_5));
  LED led_39 (.in(_7_5));
  LED led_40 (.in(_8_5));
  LED led_41 (.in(_1_7));
  LED led_42 (.in(_1_6));
  LED led_43 (.in(_2_6));
  LED led_44 (.in(_2_7));
  LED led_45 (.in(_3_7));
  LED led_46 (.in(_3_6));
  LED led_47 (.in(_4_6));
  LED led_48 (.in(_4_7));
  LED led_49 (.in(_5_6));
  LED led_50 (.in(_5_7));
  LED led_51 (.in(_6_7));
  LED led_52 (.in(_6_6));
  LED led_53 (.in(_7_6));
  LED led_54 (.in(_7_7));
  LED led_55 (.in(_8_7));
  LED led_56 (.in(_8_6));
  LED led_57 (.in(_1_8));
  LED led_58 (.in(_2_8));
  LED led_59 (.in(_3_8));
  LED led_60 (.in(_4_8));
  LED led_61 (.in(_5_8));
  LED led_62 (.in(_6_8));
  LED led_63 (.in(_7_8));
  LED led_64 (.in(_8_8));

  // Other names for the same wires on the sheet: on = in_2
endmodule

module _0_edge (
  input  in_1,
  input  in_2
);

  wire _1_1, _1_2, _1_3, _1_4, _1_5, _1_6, _1_7, _1_8, _2_1, _2_2, _2_3, _2_4, _2_5, _2_6, _2_7, _2_8, _3_1,
       _3_2, _3_3, _3_4, _3_5, _3_6, _3_7, _3_8, _4_1, _4_2, _4_3, _4_4, _4_5, _4_6, _4_7, _4_8, _5_1, _5_2,
       _5_3, _5_4, _5_5, _5_6, _5_7, _5_8, _6_1, _6_2, _6_3, _6_4, _6_5, _6_6, _6_7, _6_8, _7_1, _7_2, _7_3,
       _7_4, _7_5, _7_6, _7_7, _7_8, _8_1, _8_2, _8_3, _8_4, _8_5, _8_6, _8_7, _8_8, on;

  \cell  cell_1 (.B(_2_1), .Alive(_1_1), .BR(_2_2), .R(_1_2), .on(on));  // open: L, TL, T, TR, BL
  \cell  cell_2 (.T(_1_1), .TR(_1_2), .B(_3_2), .Alive(_2_1), .BR(_3_2), .R(_2_2), .on(on));  // open: L, TL, BL
  \cell  cell_3 (.T(_2_1), .TR(_2_2), .B(_4_1), .Alive(_3_1), .BR(_4_2), .R(_3_2), .on(on));  // open: L, TL, BL
  \cell  cell_4 (.T(_3_1), .TR(_3_2), .B(_5_1), .Alive(_4_1), .BR(_5_2), .R(_4_2), .on(on));  // open: L, TL, BL
  \cell  cell_5 (.T(_4_1), .TR(_4_2), .B(_6_1), .Alive(_5_1), .BR(_6_2), .R(_5_2), .on(on));  // open: L, TL, BL
  \cell  cell_6 (.T(_5_1), .TR(_5_2), .B(_7_1), .Alive(_6_1), .BR(_7_2), .R(_6_2), .on(on));  // open: L, TL, BL
  \cell  cell_7 (.T(_6_1), .TR(_6_2), .B(_8_1), .Alive(_7_1), .BR(_8_2), .R(_7_2), .on(on));  // open: L, TL, BL
  \cell  cell_8 (.T(_7_1), .TR(_7_2), .Alive(_8_1), .R(_8_2), .on(on));  // open: L, TL, BL, B, BR
  \cell  cell_9 (.L(_1_1), .BL(_2_1), .B(_2_2), .Alive(_1_2), .BR(_2_3), .R(_1_3), .on(on));  // open: TL, T, TR
  \cell  cell_10 (
    .L(_2_1), .TL(_1_1), .T(_1_2), .TR(_1_3), .BL(_3_1), .B(_3_2), .Alive(_2_2), .BR(_3_3), .R(_2_3), .on(on));
  \cell  cell_11 (
    .L(_3_1), .TL(_2_1), .T(_2_2), .TR(_2_3), .BL(_4_1), .B(_4_2), .Alive(_3_2), .BR(_4_3), .R(_3_3), .on(on));
  \cell  cell_12 (
    .L(_4_1), .TL(_3_1), .T(_3_2), .TR(_3_3), .BL(_5_1), .B(_5_2), .Alive(_4_2), .BR(_5_3), .R(_4_3), .on(on));
  \cell  cell_13 (
    .L(_5_1), .TL(_4_1), .T(_4_2), .TR(_4_3), .BL(_6_1), .B(_6_2), .Alive(_5_2), .BR(_6_3), .R(_5_3), .on(on));
  \cell  cell_14 (
    .L(_6_1), .TL(_5_1), .T(_5_2), .TR(_5_3), .BL(_7_1), .B(_7_2), .Alive(_6_2), .BR(_7_3), .R(_6_3), .on(on));
  \cell  cell_15 (
    .L(_7_1), .TL(_6_1), .T(_6_2), .TR(_6_3), .BL(_8_1), .B(_8_2), .Alive(_7_2), .BR(_8_3), .R(_7_3), .on(on));
  \cell  cell_16 (.L(_8_1), .TL(_7_1), .T(_7_2), .TR(_7_3), .Alive(_8_2), .R(_8_3), .on(on));  // open: BL, B, BR
  \cell  cell_17 (
    .L(_2_2), .TL(_1_2), .T(_1_3), .TR(_1_4), .BL(_3_2), .B(_3_3), .Alive(_2_3), .BR(_3_4), .R(_2_4), .on(on));
  \cell  cell_18 (
    .L(_3_2), .TL(_2_2), .T(_2_3), .TR(_2_4), .BL(_4_2), .B(_4_3), .Alive(_3_3), .BR(_4_4), .R(_3_4),
    .on(in_2));
  \cell  cell_19 (
    .L(_4_2), .TL(_3_2), .T(_3_3), .TR(_3_4), .BL(_5_2), .B(_5_3), .Alive(_4_3), .BR(_5_4), .R(_4_4), .on(on));
  \cell  cell_20 (
    .L(_5_2), .TL(_4_2), .T(_4_3), .TR(_4_4), .BL(_6_2), .B(_6_3), .Alive(_5_3), .BR(_6_4), .R(_5_4), .on(on));
  \cell  cell_21 (
    .L(_6_2), .TL(_5_2), .T(_5_3), .TR(_5_4), .BL(_7_2), .B(_7_3), .Alive(_6_3), .BR(_7_4), .R(_6_4), .on(on));
  \cell  cell_22 (
    .L(_7_2), .TL(_6_2), .T(_6_3), .TR(_6_4), .BL(_8_2), .B(_8_3), .Alive(_7_3), .BR(_8_4), .R(_7_4), .on(on));
  \cell  cell_23 (.L(_1_2), .BL(_2_2), .B(_2_3), .Alive(_1_3), .BR(_2_4), .R(_1_4), .on(on));  // open: TL, T, TR
  \cell  cell_24 (.L(_8_2), .TL(_7_2), .T(_7_3), .TR(_7_4), .Alive(_8_3), .R(_8_4), .on(on));  // open: BL, B, BR
  \cell  cell_25 (.L(_1_3), .BL(_2_3), .B(_2_4), .Alive(_1_4), .BR(_2_5), .R(_1_5), .on(on));  // open: TL, T, TR
  \cell  cell_26 (
    .L(_2_3), .TL(_1_3), .T(_1_4), .TR(_1_5), .BL(_3_3), .B(_3_4), .Alive(_2_4), .BR(_3_5), .R(_2_5), .on(on));
  \cell  cell_27 (
    .L(_3_3), .TL(_2_3), .T(_2_4), .TR(_2_5), .BL(_4_3), .B(_4_4), .Alive(_3_4), .BR(_4_5), .R(_3_5),
    .on(in_2));
  \cell  cell_28 (
    .L(_4_3), .TL(_3_3), .T(_3_4), .TR(_3_5), .BL(_5_3), .B(_5_4), .Alive(_4_4), .BR(_5_5), .R(_4_5), .on(on));
  \cell  cell_29 (
    .L(_5_3), .TL(_4_3), .T(_4_4), .TR(_4_5), .BL(_6_3), .B(_6_4), .Alive(_5_4), .BR(_6_5), .R(_5_5), .on(on));
  \cell  cell_30 (
    .L(_6_3), .TL(_5_3), .T(_5_4), .TR(_5_5), .BL(_7_3), .B(_7_4), .Alive(_6_4), .BR(_7_5), .R(_6_5), .on(on));
  \cell  cell_31 (
    .L(_7_3), .TL(_6_3), .T(_6_4), .TR(_6_5), .BL(_8_3), .B(_8_4), .Alive(_7_4), .BR(_8_5), .R(_7_5), .on(on));
  \cell  cell_32 (.L(_8_3), .TL(_7_3), .T(_7_4), .TR(_7_5), .Alive(_8_4), .R(_8_5), .on(on));  // open: BL, B, BR
  \cell  cell_33 (.L(_1_4), .BL(_2_4), .B(_2_5), .Alive(_1_5), .BR(_2_6), .R(_1_6), .on(on));  // open: TL, T, TR
  \cell  cell_34 (
    .L(_2_4), .TL(_1_4), .T(_1_5), .TR(_1_6), .BL(_3_4), .B(_3_5), .Alive(_2_5), .BR(_3_6), .R(_2_6), .on(on));
  \cell  cell_35 (
    .L(_3_4), .TL(_2_4), .T(_2_5), .TR(_2_6), .BL(_4_4), .B(_4_5), .Alive(_3_5), .BR(_4_6), .R(_3_6),
    .on(in_2));
  \cell  cell_36 (
    .L(_4_4), .TL(_3_4), .T(_3_5), .TR(_3_6), .BL(_5_4), .B(_5_5), .Alive(_4_5), .BR(_5_6), .R(_4_6), .on(on));
  \cell  cell_37 (
    .L(_5_4), .TL(_4_4), .T(_4_5), .TR(_4_6), .BL(_6_4), .B(_6_5), .Alive(_5_5), .BR(_6_6), .R(_5_6), .on(on));
  \cell  cell_38 (
    .L(_6_4), .TL(_5_4), .T(_5_5), .TR(_5_6), .BL(_7_4), .B(_7_5), .Alive(_6_5), .BR(_7_6), .R(_6_6), .on(on));
  \cell  cell_39 (
    .L(_7_4), .TL(_6_4), .T(_6_5), .TR(_6_6), .BL(_8_4), .B(_8_5), .Alive(_7_5), .BR(_8_6), .R(_7_6), .on(on));
  \cell  cell_40 (.L(_8_4), .TL(_7_4), .T(_7_5), .TR(_7_6), .Alive(_8_5), .R(_8_6), .on(on));  // open: BL, B, BR
  \cell  cell_41 (
    .L(_2_5), .TL(_1_5), .T(_1_6), .TR(_1_7), .BL(_3_5), .B(_3_6), .Alive(_2_6), .BR(_3_7), .R(_2_7), .on(on));
  \cell  cell_42 (
    .L(_3_5), .TL(_2_5), .T(_2_6), .TR(_2_7), .BL(_4_5), .B(_4_6), .Alive(_3_6), .BR(_4_7), .R(_3_7), .on(on));
  \cell  cell_43 (
    .L(_4_5), .TL(_3_5), .T(_3_6), .TR(_3_7), .BL(_5_5), .B(_5_6), .Alive(_4_6), .BR(_5_7), .R(_4_7), .on(on));
  \cell  cell_44 (
    .L(_5_5), .TL(_4_5), .T(_4_6), .TR(_4_7), .BL(_6_5), .B(_6_6), .Alive(_5_6), .BR(_6_7), .R(_5_7), .on(on));
  \cell  cell_45 (
    .L(_6_5), .TL(_5_5), .T(_5_6), .TR(_5_7), .BL(_7_5), .B(_7_6), .Alive(_6_6), .BR(_7_7), .R(_6_7), .on(on));
  \cell  cell_46 (
    .L(_7_5), .TL(_6_5), .T(_6_6), .TR(_6_7), .BL(_8_5), .B(_8_6), .Alive(_7_6), .BR(_8_7), .R(_7_7), .on(on));
  \cell  cell_47 (.L(_1_5), .BL(_2_5), .B(_2_6), .Alive(_1_6), .BR(_2_7), .R(_1_7), .on(on));  // open: TL, T, TR
  \cell  cell_48 (.L(_8_5), .TL(_7_5), .T(_7_6), .TR(_7_7), .Alive(_8_6), .R(_8_7), .on(on));  // open: BL, B, BR
  \cell  cell_49 (.L(_1_6), .BL(_2_6), .B(_2_7), .Alive(_1_7), .BR(_2_8), .R(_1_8), .on(on));  // open: TL, T, TR
  \cell  cell_50 (
    .L(_2_6), .TL(_1_6), .T(_1_7), .TR(_1_8), .BL(_3_6), .B(_3_7), .Alive(_2_7), .BR(_3_8), .R(_2_8), .on(on));
  \cell  cell_51 (
    .L(_3_6), .TL(_2_6), .T(_2_7), .TR(_2_8), .BL(_4_6), .B(_4_7), .Alive(_3_7), .BR(_4_8), .R(_3_8), .on(on));
  \cell  cell_52 (
    .L(_4_6), .TL(_3_6), .T(_3_7), .TR(_3_8), .BL(_5_6), .B(_5_7), .Alive(_4_7), .BR(_5_8), .R(_4_8), .on(on));
  \cell  cell_53 (
    .L(_5_6), .TL(_4_6), .T(_4_7), .TR(_4_8), .BL(_6_6), .B(_6_7), .Alive(_5_7), .BR(_6_8), .R(_5_8), .on(on));
  \cell  cell_54 (
    .L(_6_6), .TL(_5_6), .T(_5_7), .TR(_5_8), .BL(_7_6), .B(_7_7), .Alive(_6_7), .BR(_7_8), .R(_6_8), .on(on));
  \cell  cell_55 (
    .L(_7_6), .TL(_6_6), .T(_6_7), .TR(_6_8), .BL(_8_6), .B(_8_7), .Alive(_7_7), .BR(_8_8), .R(_7_8), .on(on));
  \cell  cell_56 (.L(_8_6), .TL(_7_6), .T(_7_7), .TR(_7_8), .Alive(_8_7), .R(_8_8), .on(on));  // open: BL, B, BR
  \cell  cell_57 (.L(_1_7), .BL(_2_7), .B(_2_8), .Alive(_1_8), .on(on));  // open: TL, T, TR, BR, R
  \cell  cell_58 (.L(_2_7), .TL(_1_7), .T(_1_8), .BL(_3_7), .B(_3_8), .Alive(_2_8), .on(on));  // open: TR, BR, R
  \cell  cell_59 (.L(_3_7), .TL(_2_7), .T(_2_8), .BL(_4_7), .B(_4_8), .Alive(_3_8), .on(on));  // open: TR, BR, R
  \cell  cell_60 (.L(_4_7), .TL(_3_7), .T(_3_8), .BL(_5_7), .B(_5_8), .Alive(_4_8), .on(on));  // open: TR, BR, R
  \cell  cell_61 (.L(_5_7), .TL(_4_7), .T(_4_8), .BL(_6_7), .B(_6_8), .Alive(_5_8), .on(on));  // open: TR, BR, R
  \cell  cell_62 (.L(_6_7), .TL(_5_7), .T(_5_8), .BL(_7_7), .B(_7_8), .Alive(_6_8), .on(on));  // open: TR, BR, R
  \cell  cell_63 (.L(_7_7), .TL(_6_7), .T(_6_8), .BL(_8_7), .B(_8_8), .Alive(_7_8), .on(on));  // open: TR, BR, R
  \cell  cell_64 (.L(_8_7), .TL(_7_7), .T(_7_8), .Alive(_8_8), .on(on));  // open: TR, BL, B, BR, R
  _0_test_fum u_0_test_fum_1 ();  // open: in_1, in_2, in_3
  LED led_1 (.in(_1_1));
  LED led_2 (.in(_2_1));
  LED led_3 (.in(_3_1));
  LED led_4 (.in(_4_1));
  LED led_5 (.in(_5_1));
  LED led_6 (.in(_6_1));
  LED led_7 (.in(_7_1));
  LED led_8 (.in(_8_1));
  LED led_9 (.in(_1_2));
  LED led_10 (.in(_2_2));
  LED led_11 (.in(_3_2));
  LED led_12 (.in(_4_2));
  LED led_13 (.in(_5_2));
  LED led_14 (.in(_6_2));
  LED led_15 (.in(_7_2));
  LED led_16 (.in(_8_2));
  LED led_17 (.in(_1_4));
  LED led_18 (.in(_1_3));
  LED led_19 (.in(_2_4));
  LED led_20 (.in(_2_3));
  LED led_21 (.in(_3_3));
  LED led_22 (.in(_3_4));
  LED led_23 (.in(_4_3));
  LED led_24 (.in(_4_4));
  LED led_25 (.in(_5_3));
  LED led_26 (.in(_5_4));
  LED led_27 (.in(_6_4));
  LED led_28 (.in(_6_3));
  LED led_29 (.in(_7_3));
  LED led_30 (.in(_7_4));
  LED led_31 (.in(_8_3));
  LED led_32 (.in(_8_4));
  LED led_33 (.in(_1_5));
  LED led_34 (.in(_2_5));
  LED led_35 (.in(_3_5));
  LED led_36 (.in(_4_5));
  LED led_37 (.in(_5_5));
  LED led_38 (.in(_6_5));
  LED led_39 (.in(_7_5));
  LED led_40 (.in(_8_5));
  LED led_41 (.in(_1_7));
  LED led_42 (.in(_1_6));
  LED led_43 (.in(_2_6));
  LED led_44 (.in(_2_7));
  LED led_45 (.in(_3_7));
  LED led_46 (.in(_3_6));
  LED led_47 (.in(_4_7));
  LED led_48 (.in(_4_6));
  LED led_49 (.in(_5_7));
  LED led_50 (.in(_5_6));
  LED led_51 (.in(_6_6));
  LED led_52 (.in(_6_7));
  LED led_53 (.in(_7_6));
  LED led_54 (.in(_7_7));
  LED led_55 (.in(_8_7));
  LED led_56 (.in(_8_6));
  LED led_57 (.in(_1_8));
  LED led_58 (.in(_2_8));
  LED led_59 (.in(_3_8));
  LED led_60 (.in(_4_8));
  LED led_61 (.in(_5_8));
  LED led_62 (.in(_6_8));
  LED led_63 (.in(_7_8));
  LED led_64 (.in(_8_8));

  // Other names for the same wires on the sheet: on1 = in_2
endmodule

module _0_test_fum (
  input  in_1,
  input  in_2,
  input  in_3
);

  wire _1_1, _1_2, _1_3, _1_4, _1_5, _1_6, _1_7, _1_8, _2_1, _2_2, _2_3, _2_4, _2_5, _2_6, _2_7, _2_8, _3_1,
       _3_2, _3_3, _3_4, _3_5, _3_6, _3_7, _3_8, _4_1, _4_2, _4_3, _4_4, _4_5, _4_6, _4_7, _4_8, _5_1, _5_2,
       _5_3, _5_4, _5_5, _5_6, _5_7, _5_8, _6_1, _6_2, _6_3, _6_4, _6_5, _6_6, _6_7, _6_8, _7_1, _7_2, _7_3,
       _7_4, _7_5, _7_6, _7_7, _7_8, _8_1, _8_2, _8_3, _8_4, _8_5, _8_6, _8_7, _8_8, clock_1_out, on1;

  \cell  cell_1 (
    .L(in_1), .TL(in_1), .T(in_1), .TR(in_1), .BL(in_1), .B(_2_1), .Alive(_1_1), .BR(_2_2), .R(_1_2),
    .on(in_3));
  \cell  cell_2 (
    .L(in_1), .TL(in_1), .T(_1_1), .TR(_1_2), .BL(in_1), .B(_3_2), .Alive(_2_1), .BR(_3_2), .R(_2_2),
    .on(in_3));
  \cell  cell_3 (
    .L(in_1), .TL(in_1), .T(_2_1), .TR(_2_2), .BL(in_1), .B(_4_1), .Alive(_3_1), .BR(_4_2), .R(_3_2),
    .on(in_3));
  \cell  cell_4 (
    .L(in_1), .TL(in_1), .T(_3_1), .TR(_3_2), .BL(in_1), .B(_5_1), .Alive(_4_1), .BR(_5_2), .R(_4_2),
    .on(in_3));
  \cell  cell_5 (
    .L(in_1), .TL(in_1), .T(_4_1), .TR(_4_2), .BL(in_1), .B(_6_1), .Alive(_5_1), .BR(_6_2), .R(_5_2),
    .on(in_3));
  \cell  cell_6 (
    .L(in_1), .TL(in_1), .T(_5_1), .TR(_5_2), .BL(in_1), .B(_7_1), .Alive(_6_1), .BR(_7_2), .R(_6_2),
    .on(in_3));
  \cell  cell_7 (
    .L(in_1), .TL(in_1), .T(_6_1), .TR(_6_2), .BL(in_1), .B(_8_1), .Alive(_7_1), .BR(_8_2), .R(_7_2), .on(on1));
  \cell  cell_8 (
    .L(in_1), .TL(in_1), .T(_7_1), .TR(_7_2), .BL(in_1), .B(in_1), .Alive(_8_1), .BR(in_1), .R(_8_2), .on(on1));
  \cell  cell_9 (
    .L(_1_1), .TL(in_1), .T(in_1), .TR(in_1), .BL(_2_1), .B(_2_2), .Alive(_1_2), .BR(_2_3), .R(_1_3),
    .on(in_3));
  \cell  cell_10 (
    .L(_2_1), .TL(_1_1), .T(_1_2), .TR(_1_3), .BL(_3_1), .B(_3_2), .Alive(_2_2), .BR(_3_3), .R(_2_3),
    .on(in_3));
  \cell  cell_11 (
    .L(_3_1), .TL(_2_1), .T(_2_2), .TR(_2_3), .BL(_4_1), .B(_4_2), .Alive(_3_2), .BR(_4_3), .R(_3_3), .on(on1));
  \cell  cell_12 (
    .L(_4_1), .TL(_3_1), .T(_3_2), .TR(_3_3), .BL(_5_1), .B(_5_2), .Alive(_4_2), .BR(_5_3), .R(_4_3), .on(on1));
  \cell  cell_13 (
    .L(_5_1), .TL(_4_1), .T(_4_2), .TR(_4_3), .BL(_6_1), .B(_6_2), .Alive(_5_2), .BR(_6_3), .R(_5_3), .on(on1));
  \cell  cell_14 (
    .L(_6_1), .TL(_5_1), .T(_5_2), .TR(_5_3), .BL(_7_1), .B(_7_2), .Alive(_6_2), .BR(_7_3), .R(_6_3),
    .on(in_3));
  \cell  cell_15 (
    .L(_7_1), .TL(_6_1), .T(_6_2), .TR(_6_3), .BL(_8_1), .B(_8_2), .Alive(_7_2), .BR(_8_3), .R(_7_3),
    .on(in_3));
  \cell  cell_16 (
    .L(_8_1), .TL(_7_1), .T(_7_2), .TR(_7_3), .BL(in_1), .B(in_1), .Alive(_8_2), .BR(in_1), .R(_8_3), .on(on1));
  \cell  cell_17 (
    .L(_1_2), .TL(in_1), .T(in_1), .TR(in_1), .BL(_2_2), .B(_2_3), .Alive(_1_3), .BR(_2_4), .R(_1_4),
    .on(in_3));
  \cell  cell_18 (
    .L(_2_2), .TL(_1_2), .T(_1_3), .TR(_1_4), .BL(_3_2), .B(_3_3), .Alive(_2_3), .BR(_3_4), .R(_2_4),
    .on(in_3));
  \cell  cell_19 (
    .L(_3_2), .TL(_2_2), .T(_2_3), .TR(_2_4), .BL(_4_2), .B(_4_3), .Alive(_3_3), .BR(_4_4), .R(_3_4),
    .on(in_3));
  \cell  cell_20 (
    .L(_4_2), .TL(_3_2), .T(_3_3), .TR(_3_4), .BL(_5_2), .B(_5_3), .Alive(_4_3), .BR(_5_4), .R(_4_4),
    .on(in_3));
  \cell  cell_21 (
    .L(_5_2), .TL(_4_2), .T(_4_3), .TR(_4_4), .BL(_6_2), .B(_6_3), .Alive(_5_3), .BR(_6_4), .R(_5_4),
    .on(in_3));
  \cell  cell_22 (
    .L(_6_2), .TL(_5_2), .T(_5_3), .TR(_5_4), .BL(_7_2), .B(_7_3), .Alive(_6_3), .BR(_7_4), .R(_6_4), .on(on1));
  \cell  cell_23 (
    .L(_7_2), .TL(_6_2), .T(_6_3), .TR(_6_4), .BL(_8_2), .B(_8_3), .Alive(_7_3), .BR(_8_4), .R(_7_4), .on(on1));
  \cell  cell_24 (
    .L(_8_2), .TL(_7_2), .T(_7_3), .TR(_7_4), .BL(in_1), .B(in_1), .Alive(_8_3), .BR(in_1), .R(_8_4),
    .on(in_3));
  \cell  cell_25 (
    .L(_1_3), .TL(in_1), .T(in_1), .TR(in_1), .BL(_2_3), .B(_2_4), .Alive(_1_4), .BR(_2_5), .R(_1_5),
    .on(in_3));
  \cell  cell_26 (
    .L(_2_3), .TL(_1_3), .T(_1_4), .TR(_1_5), .BL(_3_3), .B(_3_4), .Alive(_2_4), .BR(_3_5), .R(_2_5), .on(on1));
  \cell  cell_27 (
    .L(_3_3), .TL(_2_3), .T(_2_4), .TR(_2_5), .BL(_4_3), .B(_4_4), .Alive(_3_4), .BR(_4_5), .R(_3_5),
    .on(in_3));
  \cell  cell_28 (
    .L(_4_3), .TL(_3_3), .T(_3_4), .TR(_3_5), .BL(_5_3), .B(_5_4), .Alive(_4_4), .BR(_5_5), .R(_4_5),
    .on(in_3));
  \cell  cell_29 (
    .L(_5_3), .TL(_4_3), .T(_4_4), .TR(_4_5), .BL(_6_3), .B(_6_4), .Alive(_5_4), .BR(_6_5), .R(_5_5),
    .on(in_3));
  \cell  cell_30 (
    .L(_6_3), .TL(_5_3), .T(_5_4), .TR(_5_5), .BL(_7_3), .B(_7_4), .Alive(_6_4), .BR(_7_5), .R(_6_5),
    .on(in_3));
  \cell  cell_31 (
    .L(_7_3), .TL(_6_3), .T(_6_4), .TR(_6_5), .BL(_8_3), .B(_8_4), .Alive(_7_4), .BR(_8_5), .R(_7_5),
    .on(in_3));
  \cell  cell_32 (
    .L(_8_3), .TL(_7_3), .T(_7_4), .TR(_7_5), .BL(in_1), .B(in_1), .Alive(_8_4), .BR(in_1), .R(_8_5),
    .on(in_3));
  \cell  cell_33 (
    .L(_1_4), .TL(in_1), .T(in_1), .TR(in_1), .BL(_2_4), .B(_2_5), .Alive(_1_5), .BR(_2_6), .R(_1_6),
    .on(in_3));
  \cell  cell_34 (
    .L(_2_4), .TL(_1_4), .T(_1_5), .TR(_1_6), .BL(_3_4), .B(_3_5), .Alive(_2_5), .BR(_3_6), .R(_2_6), .on(on1));
  \cell  cell_35 (
    .L(_3_4), .TL(_2_4), .T(_2_5), .TR(_2_6), .BL(_4_4), .B(_4_5), .Alive(_3_5), .BR(_4_6), .R(_3_6),
    .on(in_3));
  \cell  cell_36 (
    .L(_4_4), .TL(_3_4), .T(_3_5), .TR(_3_6), .BL(_5_4), .B(_5_5), .Alive(_4_5), .BR(_5_6), .R(_4_6),
    .on(in_3));
  \cell  cell_37 (
    .L(_5_4), .TL(_4_4), .T(_4_5), .TR(_4_6), .BL(_6_4), .B(_6_5), .Alive(_5_5), .BR(_6_6), .R(_5_6),
    .on(in_3));
  \cell  cell_38 (
    .L(_6_4), .TL(_5_4), .T(_5_5), .TR(_5_6), .BL(_7_4), .B(_7_5), .Alive(_6_5), .BR(_7_6), .R(_6_6),
    .on(in_3));
  \cell  cell_39 (
    .L(_7_4), .TL(_6_4), .T(_6_5), .TR(_6_6), .BL(_8_4), .B(_8_5), .Alive(_7_5), .BR(_8_6), .R(_7_6),
    .on(in_3));
  \cell  cell_40 (
    .L(_8_4), .TL(_7_4), .T(_7_5), .TR(_7_6), .BL(in_1), .B(in_1), .Alive(_8_5), .BR(in_1), .R(_8_6),
    .on(in_3));
  \cell  cell_41 (
    .L(_1_5), .TL(in_1), .T(in_1), .TR(in_1), .BL(_2_5), .B(_2_6), .Alive(_1_6), .BR(_2_7), .R(_1_7),
    .on(in_3));
  \cell  cell_42 (
    .L(_2_5), .TL(_1_5), .T(_1_6), .TR(_1_7), .BL(_3_5), .B(_3_6), .Alive(_2_6), .BR(_3_7), .R(_2_7),
    .on(in_3));
  \cell  cell_43 (
    .L(_3_5), .TL(_2_5), .T(_2_6), .TR(_2_7), .BL(_4_5), .B(_4_6), .Alive(_3_6), .BR(_4_7), .R(_3_7),
    .on(in_3));
  \cell  cell_44 (
    .L(_4_5), .TL(_3_5), .T(_3_6), .TR(_3_7), .BL(_5_5), .B(_5_6), .Alive(_4_6), .BR(_5_7), .R(_4_7),
    .on(in_3));
  \cell  cell_45 (
    .L(_5_5), .TL(_4_5), .T(_4_6), .TR(_4_7), .BL(_6_5), .B(_6_6), .Alive(_5_6), .BR(_6_7), .R(_5_7),
    .on(in_3));
  \cell  cell_46 (
    .L(_6_5), .TL(_5_5), .T(_5_6), .TR(_5_7), .BL(_7_5), .B(_7_6), .Alive(_6_6), .BR(_7_7), .R(_6_7), .on(on1));
  \cell  cell_47 (
    .L(_7_5), .TL(_6_5), .T(_6_6), .TR(_6_7), .BL(_8_5), .B(_8_6), .Alive(_7_6), .BR(_8_7), .R(_7_7), .on(on1));
  \cell  cell_48 (
    .L(_8_5), .TL(_7_5), .T(_7_6), .TR(_7_7), .BL(in_1), .B(in_1), .Alive(_8_6), .BR(in_1), .R(_8_7),
    .on(in_3));
  \cell  cell_49 (
    .L(_1_6), .TL(in_1), .T(in_1), .TR(in_1), .BL(_2_6), .B(_2_7), .Alive(_1_7), .BR(_2_8), .R(_1_8),
    .on(in_3));
  \cell  cell_50 (
    .L(_2_6), .TL(_1_6), .T(_1_7), .TR(_1_8), .BL(_3_6), .B(_3_7), .Alive(_2_7), .BR(_3_8), .R(_2_8),
    .on(in_3));
  \cell  cell_51 (
    .L(_3_6), .TL(_2_6), .T(_2_7), .TR(_2_8), .BL(_4_6), .B(_4_7), .Alive(_3_7), .BR(_4_8), .R(_3_8), .on(on1));
  \cell  cell_52 (
    .L(_4_6), .TL(_3_6), .T(_3_7), .TR(_3_8), .BL(_5_6), .B(_5_7), .Alive(_4_7), .BR(_5_8), .R(_4_8), .on(on1));
  \cell  cell_53 (
    .L(_5_6), .TL(_4_6), .T(_4_7), .TR(_4_8), .BL(_6_6), .B(_6_7), .Alive(_5_7), .BR(_6_8), .R(_5_8), .on(on1));
  \cell  cell_54 (
    .L(_6_6), .TL(_5_6), .T(_5_7), .TR(_5_8), .BL(_7_6), .B(_7_7), .Alive(_6_7), .BR(_7_8), .R(_6_8),
    .on(in_3));
  \cell  cell_55 (
    .L(_7_6), .TL(_6_6), .T(_6_7), .TR(_6_8), .BL(_8_6), .B(_8_7), .Alive(_7_7), .BR(_8_8), .R(_7_8),
    .on(in_3));
  \cell  cell_56 (
    .L(_8_6), .TL(_7_6), .T(_7_7), .TR(_7_8), .BL(in_1), .B(in_1), .Alive(_8_7), .BR(in_1), .R(_8_8), .on(on1));
  \cell  cell_57 (
    .L(_1_7), .TL(in_1), .T(in_1), .TR(in_1), .BL(_2_7), .B(_2_8), .Alive(_1_8), .BR(in_1), .R(in_1),
    .on(in_3));
  \cell  cell_58 (
    .L(_2_7), .TL(_1_7), .T(_1_8), .TR(in_1), .BL(_3_7), .B(_3_8), .Alive(_2_8), .BR(in_1), .R(in_1),
    .on(in_3));
  \cell  cell_59 (
    .L(_3_7), .TL(_2_7), .T(_2_8), .TR(in_1), .BL(_4_7), .B(_4_8), .Alive(_3_8), .BR(in_1), .R(in_1),
    .on(in_3));
  \cell  cell_60 (
    .L(_4_7), .TL(_3_7), .T(_3_8), .TR(in_1), .BL(_5_7), .B(_5_8), .Alive(_4_8), .BR(in_1), .R(in_1),
    .on(in_3));
  \cell  cell_61 (
    .L(_5_7), .TL(_4_7), .T(_4_8), .TR(in_1), .BL(_6_7), .B(_6_8), .Alive(_5_8), .BR(in_1), .R(in_1),
    .on(in_3));
  \cell  cell_62 (
    .L(_6_7), .TL(_5_7), .T(_5_8), .TR(in_1), .BL(_7_7), .B(_7_8), .Alive(_6_8), .BR(in_1), .R(in_1),
    .on(in_3));
  \cell  cell_63 (
    .L(_7_7), .TL(_6_7), .T(_6_8), .TR(in_1), .BL(_8_7), .B(_8_8), .Alive(_7_8), .BR(in_1), .R(in_1), .on(on1));
  \cell  cell_64 (
    .L(_8_7), .TL(_7_7), .T(_7_8), .TR(in_1), .BL(in_1), .B(in_1), .Alive(_8_8), .BR(in_1), .R(in_1), .on(on1));
  Clock clock_1 (.out(clock_1_out));
  LED led_1 (.in(_1_1));
  LED led_2 (.in(_2_1));
  LED led_3 (.in(_3_1));
  LED led_4 (.in(_4_1));
  LED led_5 (.in(_5_1));
  LED led_6 (.in(_6_1));
  LED led_7 (.in(_7_1));
  LED led_8 (.in(_8_1));
  D_Flip_Flop d_ff_1 (.clk(clock_1_out), .D(in_2), .Q(on1), .en(clock_1_out));  // open: Qn, preset, reset
  LED led_9 (.in(_1_2));
  LED led_10 (.in(_2_2));
  LED led_11 (.in(_3_2));
  LED led_12 (.in(_4_2));
  LED led_13 (.in(_5_2));
  LED led_14 (.in(_6_2));
  LED led_15 (.in(_7_2));
  LED led_16 (.in(_8_2));
  LED led_17 (.in(_1_4));
  LED led_18 (.in(_1_3));
  LED led_19 (.in(_2_4));
  LED led_20 (.in(_2_3));
  LED led_21 (.in(_3_4));
  LED led_22 (.in(_3_3));
  LED led_23 (.in(_4_3));
  LED led_24 (.in(_4_4));
  LED led_25 (.in(_5_4));
  LED led_26 (.in(_5_3));
  LED led_27 (.in(_6_3));
  LED led_28 (.in(_7_4));
  LED led_29 (.in(_7_3));
  LED led_30 (.in(_8_4));
  LED led_31 (.in(_8_3));
  LED led_32 (.in(_1_5));
  LED led_33 (.in(_2_5));
  LED led_34 (.in(_3_5));
  LED led_35 (.in(_4_5));
  LED led_36 (.in(_5_5));
  LED led_37 (.in(_6_4));
  LED led_38 (.in(_6_5));
  LED led_39 (.in(_7_5));
  LED led_40 (.in(_8_5));
  LED led_41 (.in(_1_6));
  LED led_42 (.in(_1_7));
  LED led_43 (.in(_2_6));
  LED led_44 (.in(_2_7));
  LED led_45 (.in(_3_7));
  LED led_46 (.in(_3_6));
  LED led_47 (.in(_4_7));
  LED led_48 (.in(_4_6));
  LED led_49 (.in(_5_6));
  LED led_50 (.in(_5_7));
  LED led_51 (.in(_6_6));
  LED led_52 (.in(_7_7));
  LED led_53 (.in(_7_6));
  LED led_54 (.in(_8_7));
  LED led_55 (.in(_8_6));
  LED led_56 (.in(_1_8));
  LED led_57 (.in(_2_8));
  LED led_58 (.in(_3_8));
  LED led_59 (.in(_4_8));
  LED led_60 (.in(_5_8));
  LED led_61 (.in(_6_7));
  LED led_62 (.in(_6_8));
  LED led_63 (.in(_7_8));
  LED led_64 (.in(_8_8));

  // Other names for the same wires on the sheet: on = in_3
endmodule

module test_is_3 (
  input  TL,
  input  T,
  input  TR,
  input  L,
  input  R,
  input  BL,
  input  B,
  input  BR,
  output is_3
);

  wire and_1_out, and_2_out, and_3_out, and_4_out, and_5_out, and_6_out, and_7_out, and_8_out, and_9_out,
       and_10_out, and_11_out, and_12_out, and_13_out, and_14_out, and_15_out, and_16_out, and_17_out,
       and_18_out, and_19_out, and_20_out, and_21_out, and_22_out, and_23_out, and_24_out, and_25_out,
       and_26_out, and_27_out, and_28_out, and_29_out, and_30_out, and_31_out, and_32_out, and_33_out,
       and_34_out, and_35_out, and_36_out, and_37_out, and_38_out, and_39_out, and_40_out, and_41_out,
       and_42_out, and_43_out, and_44_out, and_45_out, and_46_out, and_47_out, and_48_out, and_49_out,
       and_50_out, and_51_out, and_52_out, and_53_out, and_54_out, and_55_out, and_56_out, xor_1_out,
       xor_2_out, xor_3_out, xor_4_out, xor_5_out, xor_6_out, xor_7_out, xor_8_out, xor_9_out, xor_10_out,
       xor_11_out, xor_12_out, xor_13_out, xor_14_out, xor_15_out, xor_16_out, xor_17_out, xor_18_out,
       xor_19_out, xor_20_out, xor_21_out, xor_22_out, xor_23_out, xor_24_out, xor_25_out, xor_26_out,
       xor_27_out, xor_28_out, xor_29_out, xor_30_out, xor_31_out, xor_32_out, xor_33_out, xor_34_out,
       xor_35_out, xor_36_out, xor_37_out, xor_38_out, xor_39_out, xor_40_out, xor_41_out, xor_42_out,
       xor_43_out, xor_44_out, xor_45_out, xor_46_out, xor_47_out, xor_48_out, xor_49_out, xor_50_out,
       xor_51_out, xor_52_out, xor_53_out, xor_54_out;

  and and_1 (and_1_out, TL, T, TR);
  and and_2 (and_2_out, TL, T, L);
  and and_3 (and_3_out, TL, T, R);
  and and_4 (and_4_out, TL, T, BL);
  and and_5 (and_5_out, TL, T, B);
  and and_6 (and_6_out, TL, T, BR);
  and and_7 (and_7_out, TL, TR, L);
  and and_8 (and_8_out, TL, TR, R);
  and and_9 (and_9_out, TL, TR, BL);
  and and_10 (and_10_out, TL, TR, B);
  and and_11 (and_11_out, TL, TR, BR);
  and and_12 (and_12_out, TL, L, R);
  and and_13 (and_13_out, TL, L, BL);
  and and_14 (and_14_out, TL, L, B);
  and and_15 (and_15_out, TL, L, BR);
  and and_16 (and_16_out, TL, R, BL);
  and and_17 (and_17_out, TL, R, B);
  and and_18 (and_18_out, TL, R, BR);
  and and_19 (and_19_out, TL, BL, B);
  and and_20 (and_20_out, TL, BL, BR);
  and and_21 (and_21_out, TL, B, BR);
  and and_22 (and_22_out, T, TR, L);
  and and_23 (and_23_out, T, TR, R);
  and and_24 (and_24_out, T, TR, BL);
  and and_25 (and_25_out, T, TR, B);
  and and_26 (and_26_out, T, TR, BR);
  and and_27 (and_27_out, T, L, R);
  and and_28 (and_28_out, T, L, BL);
  and and_29 (and_29_out, T, L, B);
  and and_30 (and_30_out, T, L, BR);
  and and_31 (and_31_out, T, R, BL);
  and and_32 (and_32_out, T, R, B);
  and and_33 (and_33_out, T, R, BR);
  and and_34 (and_34_out, T, BL, B);
  and and_35 (and_35_out, T, BL, BR);
  and and_36 (and_36_out, T, B, BR);
  and and_37 (and_37_out, TR, L, R);
  and and_38 (and_38_out, TR, L, BL);
  and and_39 (and_39_out, TR, L, B);
  and and_40 (and_40_out, TR, L, BR);
  and and_41 (and_41_out, TR, R, BL);
  and and_42 (and_42_out, TR, R, B);
  and and_43 (and_43_out, TR, R, BR);
  and and_44 (and_44_out, TR, BL, B);
  and and_45 (and_45_out, TR, BL, BR);
  and and_46 (and_46_out, TR, B, BR);
  and and_47 (and_47_out, L, R, BL);
  and and_48 (and_48_out, L, R, B);
  and and_49 (and_49_out, L, R, BR);
  and and_50 (and_50_out, L, BL, B);
  and and_51 (and_51_out, L, BL, BR);
  and and_52 (and_52_out, L, B, BR);
  and and_53 (and_53_out, R, BL, B);
  and and_54 (and_54_out, R, BL, BR);
  and and_55 (and_55_out, R, B, BR);
  and and_56 (and_56_out, BL, B, BR);
  xor xor_1 (xor_1_out, and_53_out, and_37_out);
  xor xor_2 (xor_2_out, xor_1_out, and_38_out);
  xor xor_3 (xor_3_out, xor_2_out, and_1_out);
  xor xor_4 (xor_4_out, xor_3_out, and_2_out);
  xor xor_5 (xor_5_out, xor_4_out, and_3_out);
  xor xor_6 (xor_6_out, xor_5_out, and_4_out);
  xor xor_7 (xor_7_out, xor_6_out, and_5_out);
  xor xor_8 (xor_8_out, xor_7_out, and_6_out);
  xor xor_9 (xor_9_out, xor_8_out, and_7_out);
  xor xor_10 (xor_10_out, xor_9_out, and_8_out);
  xor xor_11 (xor_11_out, xor_10_out, and_9_out);
  xor xor_12 (xor_12_out, xor_11_out, and_10_out);
  xor xor_13 (xor_13_out, xor_12_out, and_11_out);
  xor xor_14 (xor_14_out, xor_13_out, and_12_out);
  xor xor_15 (xor_15_out, xor_14_out, and_13_out);
  xor xor_16 (xor_16_out, xor_15_out, and_14_out);
  xor xor_17 (xor_17_out, xor_16_out, and_15_out);
  xor xor_18 (xor_18_out, xor_17_out, and_16_out);
  xor xor_19 (xor_19_out, xor_18_out, and_54_out);
  xor xor_20 (xor_20_out, xor_19_out, and_17_out);
  xor xor_21 (xor_21_out, xor_20_out, and_18_out);
  xor xor_22 (xor_22_out, xor_21_out, and_19_out);
  xor xor_23 (xor_23_out, xor_22_out, and_20_out);
  xor xor_24 (xor_24_out, xor_23_out, and_21_out);
  xor xor_25 (xor_25_out, xor_24_out, and_22_out);
  xor xor_26 (xor_26_out, xor_25_out, and_23_out);
  xor xor_27 (xor_27_out, xor_26_out, and_24_out);
  xor xor_28 (xor_28_out, xor_27_out, and_25_out);
  xor xor_29 (xor_29_out, xor_28_out, and_26_out);
  xor xor_30 (xor_30_out, xor_29_out, and_27_out);
  xor xor_31 (xor_31_out, xor_30_out, and_28_out);
  xor xor_32 (xor_32_out, xor_31_out, and_29_out);
  xor xor_33 (xor_33_out, xor_32_out, and_30_out);
  xor xor_34 (xor_34_out, xor_33_out, and_31_out);
  xor xor_35 (xor_35_out, xor_34_out, and_32_out);
  xor xor_36 (xor_36_out, xor_35_out, and_33_out);
  xor xor_37 (xor_37_out, xor_36_out, and_34_out);
  xor xor_38 (xor_38_out, xor_37_out, and_35_out);
  xor xor_39 (xor_39_out, xor_38_out, and_36_out);
  xor xor_40 (xor_40_out, xor_39_out, and_39_out);
  xor xor_41 (xor_41_out, xor_40_out, and_40_out);
  xor xor_42 (xor_42_out, xor_41_out, and_55_out);
  xor xor_43 (xor_43_out, xor_42_out, and_42_out);
  xor xor_44 (xor_44_out, xor_43_out, and_43_out);
  xor xor_45 (xor_45_out, xor_44_out, and_44_out);
  xor xor_46 (xor_46_out, xor_45_out, and_45_out);
  xor xor_47 (xor_47_out, xor_46_out, and_46_out);
  xor xor_48 (xor_48_out, xor_47_out, and_47_out);
  xor xor_49 (xor_49_out, xor_48_out, and_48_out);
  xor xor_50 (xor_50_out, xor_49_out, and_49_out);
  xor xor_51 (xor_51_out, xor_50_out, and_50_out);
  xor xor_52 (xor_52_out, xor_51_out, and_51_out);
  xor xor_53 (xor_53_out, xor_52_out, and_52_out);
  xor xor_54 (xor_54_out, xor_53_out, and_41_out);
  xor xor_55 (is_3, xor_54_out, and_56_out);
endmodule
